// Logisim project ula.circ as structural Verilog: 3 circuits, main circuit full-adder
module full_adder (
  input  A,
  input  B,
  input  Cin,
  output S,
  output Cout
);

  wire and_1_out, and_2_out, xnor_1_out;

  xnor xnor_1 (xnor_1_out, A, B);
  and and_1 (and_1_out, Cin, xnor_1_out);
  and and_2 (and_2_out, B, A);
  xnor xnor_2 (S, xnor_1_out, Cin);
  or or_1 (Cout, and_1_out, and_2_out);
endmodule

module \xor  (
  input  [3:0] A,
  input  in_2,
  input  [3:0] B,
  output [3:0] AxorB
);

  wire xor_1_out, xor_2_out, xor_3_out, xor_4_out;

  xor xor_1 (xor_1_out, A[0], B[0]);
  xor xor_2 (xor_2_out, A[1], B[1]);
  xor xor_3 (xor_3_out, A[2], B[2]);
  xor xor_4 (xor_4_out, A[3], B[3]);
  and and_1 (AxorB[0], xor_1_out, in_2);
  and and_2 (AxorB[1], xor_2_out, in_2);
  and and_3 (AxorB[2], xor_3_out, in_2);
  and and_4 (AxorB[3], xor_4_out, in_2);
endmodule

module M (
  input  OP,
  input  Sinal,
  input  Overflow,
  output Erro,
  output Sinal_2,
  output Overflow_2
);

  and and_1 (Erro, ~OP, Overflow, Sinal);  // AND_Gate

  assign Overflow_2 = Overflow;
  assign Sinal_2 = Sinal;
endmodule
